# Fritzing sketch HologramDashWeatherStation (saved by Fritzing 0.9.3b)
breadboards: 1

parts:
  Q1 = MOSFET-NCHANNEL [package=to220v]  # not connected
  Q2 = MOSFET-NCHANNEL [package=to220v]  # not connected
  Part3 = Adafruit_BMP280
  Part4 = Dash
  DHT1 = DHT22 Humidity and Temperature Sensor
  J1 = RJ11 Jack [package=rj11-6]
  R1 = Resistor [tolerance=±5% resistance=10k package=THT]
  U1 = LIPO-2000mAh [package=lipo-2000]
  Part5 = Adafruit USB DC Solar LiPo Charger [part_number="Adafruit #390"]
  Part6 = Solar Cell

nets:
  GND: Part3.GND, Part4.GND#1, U1.-, Part5.GND, Part6.-
  N1: Part3.CS, Part4.CTX
  N2: Part4.VBATT, DHT1.VDD, J1.2, R1.Pin_0
  N3: Part4.GND#19, DHT1.GND, J1.3
  N4: Part4.TX, DHT1.DATA, R1.Pin_1
  N5: Part4.D02, J1.1
  N6: U1.+, Part5.BATT
  N7: Part5.DCIN, Part6.+

custom parts:
  Adafruit_BMP280: Bosch has stepped up their game with their new BMP280 sensor, an environmental sensor with temperature, barometric pressure that is the next generation upgrade to the BMP085/BMP180/BMP183. This sensor is great for all sorts of weather sensing and can even be used in both I2C and SPI! This precision sensor from Bosch is the best low-cost, precision sensing solution for measuring barometric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
  Dash: The Hologram Dash is a cellular development kit for rapid application development. It can be used for prototyping, as cellular gateways, or as modules embedded within a final product. Because the hardware and firmware are open source, the Hologram Dash can scale with your production, even to the point of embedding the reference design within your own designs.
  Adafruit USB DC Solar LiPo Charger: Make your projects to go green this summer with our specialized USB/Solar Lithium Ion Polymer Battery charger! This charger is a very unique design, perfect for outdoor projects, or DIY iPod chargers. We've spent over a year testing and tinkering with this charger to come up with a plug and play solution to charging batteries with the sun and we're really pleased with what we ended up with.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
