# Fritzing sketch ElectronHardwareLayout (saved by Fritzing 0.9.3b)
circuit board: 8.46667cm x 5.64444cm
breadboards: 1

parts:
  J1 = RJ11 Jack [package=rj11-6]
  Part1 = Electron
  DHT1 = DHT22 Humidity and Temperature Sensor
  Part3 = Solar Cell
  Part4 = Sunny Buddy MPPT LiPo Charger
  R1 = Resistor [tolerance=±5% resistance=10k package=THT]
  Q2 = NPN-Transistor [package="TO92 [THT]"]
  R2 = Resistor [tolerance=±5% resistance=100k package=THT]
  R3 = TRIMPOT [package=trimpot_pth_s3_lock]
  U1 = LIPO-2000mAh [package=lipo-2000]
  Part5 = GY-BMEP280 Barometric Pressure Sensor - Breakout

nets:
  N1: J1.1, Part1.C1
  N2: J1.2, Part4.Load_+_(.1"_Header)
  GND: J1.3, Part1.GND, Part4.Load_-_(.1"_Header), Q2.C, U1.-, Part5.GND
  N3: Part1.D0, Part5.SDA
  N4: Part1.D1, Part5.SCL
  N5: Part1.D6, DHT1.DATA
  3V3: Part1.3V3, DHT1.VDD, Part5.VCC
  N6: Part1.B5, R3.WIPER
  N7: Part1.C0, R1.Pin_1
  N8: DHT1.GND, Q2.E, R3.CW
  N9: Part3.+, Part4.Secondary_+, R2.Pin_0
  N10: Part3.-, Part4.Secondary_-
  N11: R1.Pin_0, Q2.B
  N12: R2.Pin_1, R3.CCW

custom parts:
  Sunny Buddy MPPT LiPo Charger: Switch-mode MPPT charger for single cell LiPo batteries. Accepts up to 20V solar cell input.
  GY-BMEP280 Barometric Pressure Sensor - Breakout: The BME280 is a chip which was originally designed for the next generation of smartphones. It is made up of a very accurate pressure sensor and an associated temperature sensor which helps calibrate the pressure readings. And just for fun they threw in a pretty solid humidity sensor in there as well! So with an I2C connection you have access to enough weather data to make some pretty good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
