# Fritzing sketch HardwareLayout (saved by Fritzing 0.9.3b)
breadboards: 1

parts:
  Part1 = INA219 High Side DC Current Sensor Breakout [part_number=904]  # not connected
  Part2 = Adafruit BME280
  U1 = attiny85 [package=dip]
  Part3 = Triple Axis Magnetometer - HMC5883 Breakout  # not connected
  J1 = RJ11 Jack [package=rj11-6]  # not connected
  Part4 = Adafruit HUZZAH32 ESP32 Feather [part_number="Adafruit #3405"]  # not connected
  Part5 = Adafruit Feather 32u4 Basic Proto [part_number="Adafruit #2771"]
  U2 = LIPO-2000mAh [package=lipo-2000]
  Part6 = Solar Cell  # not connected
  R1 = Resistor [tolerance=±5% resistance=10k package="1206 [SMD]"]
  R2 = Resistor [tolerance=±5% resistance=10k package="1206 [SMD]"]

nets:
  N1: Part2.3.3V, R1.Pin_0, R2.Pin_0
  N2: Part2.GND, U1.Pin_4, U2.-
  N3: Part2.SCK/SCL, U1.Pin_5, Part5.2, R1.Pin_1
  N4: Part2.SDO/ADR, U1.Pin_7, Part5.3, R2.Pin_1
  N5: U1.Pin_8, Part5.VBAT, U2.+

custom parts:
  INA219 High Side DC Current Sensor Breakout: This breakout board will solve all your power-monitoring problems. Instead of struggling with two multimeters, you can just use the handy INA219B chip on this breakout to both measure both the high side voltage and DC current draw over I2C with 1% precision. Most current-measuring devices such as our current panel meter are only good for low side measuring. That means that unless you want to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
  Adafruit BME280: Bosch has stepped up their game with their new BME280 sensor, an environmental sensor with temperature, barometric pressure and humidity! This sensor is great for all sorts of weather/environmental sensing and can even be used in both I2C and SPI! This precision sensor from Bosch is the best low-cost sensing solution for measuring humidity with ±3% accuracy, barometric pressure with ±1 hPa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
  Adafruit Feather 32u4 Basic Proto: At the Feather 32u4's heart is at ATmega32u4 clocked at 8 MHz and at 3.3V logic, a chip setup we've had tons of experience with as it's the same as the Flora. This chip has 32K of flash and 2K of RAM, with built in USB so not only does it have a USB-to-Serial program & debug capability built in with no need for an FTDI-like chip, it can also act like a mouse, keyboard, USB MIDI device, etc.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
