# Fritzing sketch Schematic (saved by Fritzing 0.9.3b)
circuit board: 8.46667cm x 5.64444cm
breadboards: 1

parts:
  J1 = RJ11 Jack [package=rj11-6]
  Part1 = Electron
  Part2 = Adafruit_BMP280
  DHT1 = DHT22 Humidity and Temperature Sensor
  Part3 = Solar Cell
  Part4 = Sunny Buddy MPPT LiPo Charger
  R1 = Resistor [tolerance=±5% resistance=10k package=THT]
  Q2 = NPN-Transistor [package="TO92 [THT]"]
  R2 = Resistor [tolerance=±5% resistance=100k package=THT]
  R3 = TRIMPOT [package=trimpot_pth_s3_lock]
  U1 = LIPO-2000mAh [package=lipo-2000]

nets:
  N1: J1.1, Part1.C1
  N2: J1.2, Part4.Load_+_(.1"_Header)
  GND: J1.3, Part1.GND, Part2.GND, Part4.Load_-_(.1"_Header), Q2.C, U1.-
  N3: Part1.A1, Part2.CS
  N4: Part1.A2, Part2.SCK/SCL
  N5: Part1.A3, Part2.SDO/ADR
  N6: Part1.A4, Part2.SDI/SDA
  N7: Part1.D6, DHT1.DATA
  3V3: Part1.3V3, Part2.VIN, DHT1.VDD
  N8: Part1.B5, R3.WIPER
  N9: Part1.C0, R1.Pin_1
  N10: DHT1.GND, Q2.E, R3.CW
  N11: Part3.+, Part4.Secondary_+, R2.Pin_0
  N12: Part3.-, Part4.Secondary_-
  N13: R1.Pin_0, Q2.B
  N14: R2.Pin_1, R3.CCW

custom parts:
  Adafruit_BMP280: Bosch has stepped up their game with their new BMP280 sensor, an environmental sensor with temperature, barometric pressure that is the next generation upgrade to the BMP085/BMP180/BMP183. This sensor is great for all sorts of weather sensing and can even be used in both I2C and SPI! This precision sensor from Bosch is the best low-cost, precision sensing solution for measuring barometric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
  Sunny Buddy MPPT LiPo Charger: Switch-mode MPPT charger for single cell LiPo batteries. Accepts up to 20V solar cell input.
